// Logisim project buttons.circ as structural Verilog: 1 circuit, main circuit snes_buttons
module snes_buttons (
  output start_button,
  output select_button,
  output left_button,
  output right_button,
  output up_button,
  output down_button,
  output x_button,
  output y_button,
  output a_button,
  output b_button,
  output l_button,
  output r_button
);


  assign a_button = 1'b0;
  assign b_button = 1'b0;
  assign down_button = 1'b0;
  assign l_button = 1'b0;
  assign left_button = 1'b0;
  assign r_button = 1'b0;
  assign right_button = 1'b0;
  assign select_button = 1'b0;
  assign start_button = 1'b0;
  assign up_button = 1'b0;
  assign x_button = 1'b0;
  assign y_button = 1'b0;
endmodule
