// Logisim project snazzy.circ as structural Verilog: 8 circuits, main circuit main
module main (
  input  in_1,
  output SNES_data1,
  output SNES_clack,
  output halt,
  output SNES_latch
);

  wire cd4021b_1_q8, clock_1_out, nand_1_out, nand_2_out, nand_3_out, nand_4_out, not_1_out, not_2_out,
       not_3_out, not_4_out, not_5_out, not_6_out, not_7_out, not_8_out, not_9_out, not_10_out, not_11_out,
       not_12_out, not_13_out, not_14_out, not_15_out, not_16_out, snes_buttons_1_a_button,
       snes_buttons_1_b_button, snes_buttons_1_down_button, snes_buttons_1_l_button,
       snes_buttons_1_left_button, snes_buttons_1_r_button, snes_buttons_1_right_button,
       snes_buttons_1_select_button, snes_buttons_1_start_button, snes_buttons_1_up_button,
       snes_buttons_1_x_button, snes_buttons_1_y_button;
  wire [7:0] snes_1_round;

  SNES snes_1 (
    .CLACK(SNES_clack), .LATCH(SNES_latch), .ROUND({snes_1_round[7:2], halt, snes_1_round[0]}), .RESET(in_1));  // open: DATA1
  CD4021B cd4021b_1 (
    .Q8(cd4021b_1_q8), .CL(SNES_clack), .PSC(SNES_latch), .P1(1'b1), .P2(1'b1), .P3(1'b1), .P4(1'b1),
    .P5(not_4_out), .P6(not_1_out), .P7(not_3_out), .P8(not_2_out));  // open: Q6, Q7, SI
  not not_1 (not_1_out, snes_buttons_1_l_button);
  not not_2 (not_2_out, snes_buttons_1_a_button);
  not not_3 (not_3_out, snes_buttons_1_x_button);
  not not_4 (not_4_out, snes_buttons_1_r_button);
  not not_5 (not_5_out, snes_buttons_1_b_button);
  not not_6 (not_6_out, snes_buttons_1_y_button);
  not not_7 (not_7_out, snes_buttons_1_down_button);
  snes_buttons snes_buttons_1 (
    .start_button(snes_buttons_1_start_button), .select_button(snes_buttons_1_select_button),
    .left_button(snes_buttons_1_left_button), .right_button(snes_buttons_1_right_button),
    .up_button(snes_buttons_1_up_button), .down_button(snes_buttons_1_down_button),
    .x_button(snes_buttons_1_x_button), .y_button(snes_buttons_1_y_button),
    .a_button(snes_buttons_1_a_button), .b_button(snes_buttons_1_b_button),
    .l_button(snes_buttons_1_l_button), .r_button(snes_buttons_1_r_button));
  not not_8 (not_8_out, snes_buttons_1_up_button);
  not not_9 (not_9_out, snes_buttons_1_left_button);
  not not_10 (not_10_out, snes_buttons_1_start_button);
  not not_11 (not_11_out, snes_buttons_1_right_button);
  not not_12 (not_12_out, snes_buttons_1_select_button);
  not not_13 (not_13_out, not_8_out);
  nand nand_1 (nand_1_out, not_13_out, not_7_out);
  not not_14 (not_14_out, not_9_out);
  nand nand_2 (nand_2_out, not_14_out, not_11_out);
  CD4021B cd4021b_2 (
    .Q8(SNES_data1), .SI(cd4021b_1_q8), .CL(SNES_clack), .PSC(SNES_latch), .P1(nand_4_out), .P2(nand_2_out),
    .P3(nand_3_out), .P4(nand_1_out), .P5(not_10_out), .P6(not_12_out), .P7(not_6_out), .P8(not_5_out));  // open: Q6, Q7
  not not_15 (not_15_out, not_7_out);
  nand nand_3 (nand_3_out, not_8_out, not_15_out);
  not not_16 (not_16_out, not_11_out);
  nand nand_4 (nand_4_out, not_9_out, not_16_out);
  Clock clock_1 (.out(clock_1_out));
  // Digital_Oscilloscope digital_oscilloscope_1: pin names not known; wires that end beside it: clock_1_out, SNES_clack, SNES_latch, SNES_data1

  // Notes on the sheet:
  //   clock
  //   SNES_clack
  //   SNES_latch
  //   SNES_data1
endmodule

module CD4021B_dff (
  input  in_1,
  input  P,
  input  nD,
  input  PS,
  output nQ
);

  wire nCL, not_1_out, not_3_out, transmission_1_p4, transmission_3_p4, transmission_4_p4, transmission_5_p4,
       transmission_6_p4;

  not not_1 (not_1_out, PS);
  // Transmission_Gate transmission_1: pin names not known; wires that end beside it: P, PS, not_1_out, transmission_1_p4
  // Transmission_Gate transmission_2: pin names not known; wires that end beside it: nD, not_1_out, PS, transmission_1_p4
  // Transmission_Gate transmission_3: pin names not known; wires that end beside it: transmission_1_p4, in_1, nCL, transmission_3_p4
  not not_2 (nCL, in_1);
  not not_3 (not_3_out, transmission_3_p4);
  // Transmission_Gate transmission_4: pin names not known; wires that end beside it: transmission_3_p4, nCL, in_1, transmission_4_p4
  not not_4 (transmission_4_p4, not_3_out);
  // Transmission_Gate transmission_5: pin names not known; wires that end beside it: not_3_out, nCL, in_1, transmission_5_p4
  // Transmission_Gate transmission_6: pin names not known; wires that end beside it: transmission_5_p4, in_1, nCL, transmission_6_p4
  not not_5 (transmission_6_p4, nQ);
  not not_6 (nQ, transmission_5_p4);

  // Other names for the same wires on the sheet: CL = in_1
endmodule

module CD4021B (
  input  P1,
  input  P2,
  input  P3,
  input  P4,
  input  P5,
  input  P6,
  input  P7,
  input  P8,
  input  SI,
  input  CL,
  input  PSC,
  output Q6,
  output Q7,
  output Q8
);

  wire cd4021b_dff_simple_1_nq, cd4021b_dff_simple_2_nq, cd4021b_dff_simple_3_nq, cd4021b_dff_simple_4_nq,
       cd4021b_dff_simple_5_nq, cd4021b_dff_simple_6_nq, cd4021b_dff_simple_7_nq, cd4021b_dff_simple_8_nq,
       nand_1_out, not_1_out, not_2_out, not_3_out, not_4_out, not_5_out, not_6_out, not_7_out, not_8_out,
       not_9_out, not_10_out, not_11_out, not_13_out, not_14_out;

  not not_1 (not_1_out, SI);
  not not_2 (not_2_out, PSC);
  not not_3 (not_3_out, not_1_out);
  not not_4 (not_4_out, not_3_out);
  not not_5 (not_5_out, CL);
  nand nand_1 (nand_1_out, not_5_out, not_2_out);
  not not_6 (not_6_out, P1);
  // Probe on cd4021b_dff_simple_1_nq
  not not_7 (not_7_out, P2);
  CD4021B_dff_simple cd4021b_dff_simple_1 (
    .nQ(cd4021b_dff_simple_1_nq), .P(not_6_out), .PS(not_2_out), .nD(not_4_out), .CL(nand_1_out));
  // Probe on cd4021b_dff_simple_2_nq
  CD4021B_dff_simple cd4021b_dff_simple_2 (
    .nQ(cd4021b_dff_simple_2_nq), .P(not_7_out), .PS(not_2_out), .nD(cd4021b_dff_simple_1_nq), .CL(nand_1_out));
  // Probe on cd4021b_dff_simple_3_nq
  not not_8 (not_8_out, P3);
  CD4021B_dff_simple cd4021b_dff_simple_3 (
    .nQ(cd4021b_dff_simple_3_nq), .P(not_8_out), .PS(not_2_out), .nD(cd4021b_dff_simple_2_nq), .CL(nand_1_out));
  // Probe on cd4021b_dff_simple_4_nq
  not not_9 (not_9_out, P4);
  CD4021B_dff_simple cd4021b_dff_simple_4 (
    .nQ(cd4021b_dff_simple_4_nq), .P(not_9_out), .PS(not_2_out), .nD(cd4021b_dff_simple_3_nq), .CL(nand_1_out));
  // Probe on cd4021b_dff_simple_5_nq
  not not_10 (not_10_out, P5);
  CD4021B_dff_simple cd4021b_dff_simple_5 (
    .nQ(cd4021b_dff_simple_5_nq), .P(not_10_out), .PS(not_2_out), .nD(cd4021b_dff_simple_4_nq),
    .CL(nand_1_out));
  // Probe on cd4021b_dff_simple_6_nq
  not not_11 (not_11_out, P6);
  CD4021B_dff_simple cd4021b_dff_simple_6 (
    .nQ(cd4021b_dff_simple_6_nq), .P(not_11_out), .PS(not_2_out), .nD(cd4021b_dff_simple_5_nq),
    .CL(nand_1_out));
  not not_12 (Q6, cd4021b_dff_simple_6_nq);
  not not_13 (not_13_out, P7);
  CD4021B_dff_simple cd4021b_dff_simple_7 (
    .nQ(cd4021b_dff_simple_7_nq), .P(not_13_out), .PS(not_2_out), .nD(cd4021b_dff_simple_6_nq),
    .CL(nand_1_out));
  // Probe on cd4021b_dff_simple_7_nq
  not not_14 (not_14_out, P8);
  not not_15 (Q7, cd4021b_dff_simple_7_nq);
  // Probe on cd4021b_dff_simple_8_nq
  CD4021B_dff_simple cd4021b_dff_simple_8 (
    .nQ(cd4021b_dff_simple_8_nq), .P(not_14_out), .PS(not_2_out), .nD(cd4021b_dff_simple_7_nq),
    .CL(nand_1_out));
  not not_16 (Q8, cd4021b_dff_simple_8_nq);
endmodule

module CD4021B_dff_simple (
  input  P,
  input  PS,
  input  nD,
  input  CL,
  output nQ
);

  wire and_1_out, and_2_out, d_ff_1_q, not_1_out, not_2_out, not_3_out, not_4_out;

  not not_1 (not_1_out, P);
  not not_2 (not_2_out, PS);
  not not_3 (not_3_out, not_1_out);
  and and_1 (and_1_out, not_1_out, not_2_out);
  D_Flip_Flop d_ff_1 (.D(not_4_out), .clk(CL), .Q(d_ff_1_q), .Qn(nQ), .preset(and_1_out), .reset(and_2_out));
  not not_4 (not_4_out, nD);
  and and_2 (and_2_out, not_3_out, not_2_out);
  // NoConnect on d_ff_1_q
endmodule

module CD4021B_dff2 (
  input  in_1,
  input  P,
  input  nD,
  input  PS,
  output nQ
);

  wire nCL, not_1_out, not_4_out, transmission_1_p4, transmission_2_p4, transmission_4_p4, transmission_5_p4,
       transmission_6_p4;

  not not_1 (not_1_out, PS);
  // Transmission_Gate transmission_1: pin names not known; wires that end beside it: P, PS, not_1_out, transmission_1_p4
  // Transmission_Gate transmission_2: pin names not known; wires that end beside it: nD, in_1, nCL, transmission_2_p4
  // Transmission_Gate transmission_3: pin names not known; wires that end beside it: transmission_2_p4, not_1_out, PS, transmission_1_p4
  // Transmission_Gate transmission_4: pin names not known; wires that end beside it: transmission_2_p4, nCL, in_1, transmission_4_p4
  not not_2 (nCL, in_1);
  not not_3 (transmission_4_p4, not_4_out);
  not not_4 (not_4_out, transmission_1_p4);
  // Transmission_Gate transmission_5: pin names not known; wires that end beside it: not_4_out, nCL, in_1, transmission_5_p4
  not not_5 (nQ, transmission_5_p4);
  // Transmission_Gate transmission_6: pin names not known; wires that end beside it: transmission_5_p4, in_1, nCL, transmission_6_p4
  not not_6 (transmission_6_p4, nQ);

  // Other names for the same wires on the sheet: CL = in_1
endmodule

module MC14021B (
  input  P1,
  input  in_2,
  input  in_3,
  input  in_4,
  input  in_5,
  input  in_6,
  input  in_7,
  input  in_8,
  input  PS,
  input  DS,
  input  CLOCK,
  output Q6,
  output Q7,
  output Q8
);

  wire mc14021b_dff_1_q, mc14021b_dff_2_q, mc14021b_dff_3_q, mc14021b_dff_4_q, mc14021b_dff_5_q,
       mc14021b_dff_6_nq, mc14021b_dff_6_q, mc14021b_dff_7_nq, mc14021b_dff_7_q, mc14021b_dff_8_nq,
       mc14021b_dff_8_q, nand_1_out, not_1_out, not_2_out, not_3_out, not_4_out, not_5_out;

  not not_1 (not_1_out, PS);
  not not_2 (not_2_out, not_1_out);
  not not_3 (not_3_out, DS);
  not not_4 (not_4_out, not_3_out);
  not not_5 (not_5_out, CLOCK);
  nand nand_1 (nand_1_out, not_1_out, not_5_out);
  MC14021B_dff mc14021b_dff_1 (
    .Q(mc14021b_dff_1_q), .P(P1), .PS(not_2_out), .D(not_4_out), .CLOCK(nand_1_out));  // open: nQ
  MC14021B_dff mc14021b_dff_2 (
    .Q(mc14021b_dff_2_q), .P(in_2), .PS(not_2_out), .D(mc14021b_dff_1_q), .CLOCK(nand_1_out));  // open: nQ
  MC14021B_dff mc14021b_dff_3 (
    .Q(mc14021b_dff_3_q), .P(in_3), .PS(not_2_out), .D(mc14021b_dff_2_q), .CLOCK(nand_1_out));  // open: nQ
  MC14021B_dff mc14021b_dff_4 (
    .Q(mc14021b_dff_4_q), .P(in_4), .PS(not_2_out), .D(mc14021b_dff_3_q), .CLOCK(nand_1_out));  // open: nQ
  MC14021B_dff mc14021b_dff_5 (
    .Q(mc14021b_dff_5_q), .P(in_5), .PS(not_2_out), .D(mc14021b_dff_4_q), .CLOCK(nand_1_out));  // open: nQ
  MC14021B_dff mc14021b_dff_6 (
    .Q(mc14021b_dff_6_q), .nQ(mc14021b_dff_6_nq), .P(in_6), .PS(not_2_out), .D(mc14021b_dff_5_q),
    .CLOCK(nand_1_out));
  not not_6 (Q6, mc14021b_dff_6_nq);
  MC14021B_dff mc14021b_dff_7 (
    .Q(mc14021b_dff_7_q), .nQ(mc14021b_dff_7_nq), .P(in_7), .PS(not_2_out), .D(mc14021b_dff_6_q),
    .CLOCK(nand_1_out));
  not not_7 (Q7, mc14021b_dff_7_nq);
  // NoConnect on mc14021b_dff_8_q
  MC14021B_dff mc14021b_dff_8 (
    .Q(mc14021b_dff_8_q), .nQ(mc14021b_dff_8_nq), .P(in_8), .PS(not_2_out), .D(mc14021b_dff_7_q),
    .CLOCK(nand_1_out));
  not not_8 (Q8, mc14021b_dff_8_nq);
endmodule

module MC14021B_dff (
  input  P,
  input  PS,
  input  D,
  input  CLOCK,
  output Q,
  output nQ
);

  wire and_1_out, and_2_out, not_1_out;

  not not_1 (not_1_out, P);
  and and_1 (and_1_out, P, PS);
  D_Flip_Flop d_ff_1 (.D(D), .clk(CLOCK), .Q(Q), .Qn(nQ), .preset(and_1_out), .reset(and_2_out));
  and and_2 (and_2_out, not_1_out, PS);
endmodule

module SNES (
  input  RESET,
  input  DATA1,
  output [7:0] ROUND,
  output CLACK,
  output LATCH
);

  wire clock_1_out, counter_1_carry;
  wire [5:0] counter_1_q;

  Clock clock_1 (.out(clock_1_out));
  Counter #(.max('h3f), .width(6)) counter_1 (
    .clr(RESET), .clk(clock_1_out), .carry(counter_1_carry), .Q(counter_1_q));  // open: load, up, count, D
  // NoConnect on DATA1
  Counter counter_2 (.clk(counter_1_carry), .Q(ROUND));  // open: clr, load, up, count, D, carry
  PLA #(.in_width(6), .\table ("000000 01 # init\n000001 11 # latch on\n000010 11\n000011 01 # latch off\n000100 00 # start clock: B\n000101 01\n000110 00 # Y\n000111 01\n001000 00 # select\n001001 01\n001010 00 # start\n001011 01\n001100 00 # up\n001101 01\n001110 00 # down\n001111 01\n010000 00 # left\n010001 01\n010010 00 # right\n010011 01\n010100 00 # A\n010101 01\n010110 00 # X\n010111 01\n011000 00 # L\n011001 01\n011010 00 # R\n011011 01\n011100 00 # (high)\n011101 01\n011110 00 # (high)\n011111 01\n100000 00 # (high)\n100001 01\n100010 00 # (high)\n100011 01 # end clock\n100100 01\n100101 01\n100110 01\n100111 01\n101xxx 01 # (padding)\n11xxxx 01 # (padding)")) pla_1 (
    .in(counter_1_q), .out({LATCH, CLACK}));
  // Digital_Oscilloscope digital_oscilloscope_1: pin names not known; wires that end beside it: clock_1_out, CLACK, LATCH
endmodule
